# Fritzing sketch MorseSeinenOntwerp (saved by Fritzing 0.9.2b)
breadboards: 3

parts:
  Part3 = Arduino Uno (Rev3)
  S5 = Pushbutton [package="[THT]"]
  S6 = Pushbutton [package="[THT]"]
  S7 = Pushbutton [package="[SMD]"]
  S8 = Pushbutton [package="[THT]"]
  R13 = Resistor [tolerance=±5% resistance=220 package=THT]
  R14 = Resistor [tolerance=±5% resistance=220 package=THT]
  R15 = Resistor [tolerance=±5% resistance=220 package=THT]
  R16 = Resistor [tolerance=±5% resistance=220 package=THT]
  R17 = Resistor [tolerance=±5% resistance=220 package=THT]
  LED1 = LED - 3mm [color="Red (633nm)" package="3 mm [THT]"]
  LCD1 = LCD screen
  R19 = Resistor [tolerance=±5% resistance=220 package=THT]
  Part4 = Arduino Uno (Rev3)
  S9 = Pushbutton [package="[THT]"]
  R20 = Resistor [tolerance=±5% resistance=220 package=THT]
  R21 = Resistor [tolerance=±5% resistance=220 package=THT]
  R22 = Resistor [tolerance=±5% resistance=220 package=THT]
  R23 = Resistor [tolerance=±5% resistance=220 package=THT]
  R24 = Resistor [tolerance=±5% resistance=220 package=THT]
  R25 = Resistor [tolerance=±5% resistance=220 package=THT]
  S10 = Pushbutton [package="[THT]"]
  S11 = Pushbutton [package="[SMD]"]
  S12 = Pushbutton [package="[THT]"]
  LED2 = LED - 3mm [color="Red (633nm)" package="3 mm [THT]"]
  LCD2 = LCD screen
  R26 = Rotary Potentiometer (Large) [maximum_resistance=100kΩ package=THT]
  R18 = Rotary Potentiometer (Large) [maximum_resistance=100kΩ package=THT]

nets:
  N1: Part3.A4/SDA, Part4.A4/SDA
  N2: Part3.A5/SCL, Part4.A5/SCL
  N3: Part3.D8, Part4.D9_PWM
  N4: Part3.D9_PWM, Part4.D8
  N5: Part3.D10_PWM/SS, S7.Pin_1, S7.Pin_2, R16.Pin_1
  N6: Part3.D11_PWM/MOSI, S6.Pin_1, S6.Pin_2, R15.Pin_1
  N7: Part3.D12/MISO, S5.Pin_1, S5.Pin_2, R14.Pin_1
  N8: Part3.D13/SCK, S8.Pin_1, S8.Pin_2, R13.Pin_1
  GND: Part3.GND, R13.Pin_0, R14.Pin_0, R15.Pin_0, R16.Pin_0, R17.Pin_0, LCD1.VSS, LCD1.R/W, LCD1.LED-, Part4.GND, R20.Pin_0, R21.Pin_0, R22.Pin_0, R23.Pin_0, R25.Pin_0, LCD2.VSS, LCD2.R/W, LCD2.LED-, R26.leg2, R18.leg2
  N9: Part3.D1/TX, LED1.anode
  N10: Part3.D2, LCD1.DB7
  N11: Part3.D3_PWM, LCD1.DB6
  N12: Part3.D4, LCD1.DB5
  N13: Part3.D5_PWM, LCD1.DB4
  N14: Part3.D6_PWM, LCD1.RS
  N15: Part3.D7, LCD1.E
  5V: Part3.5V, S5.Pin_3, S5.Pin_4, S6.Pin_3, S6.Pin_4, S7.Pin_3, S7.Pin_4, S8.Pin_3, S8.Pin_4, LCD1.VDD, R19.Pin_1, R18.leg1
  N16: R17.Pin_1, LED1.cathode
  N17: LCD1.V0, R18.wiper
  N18: LCD1.LED+, R19.Pin_0
  N19: Part4.D10_PWM/SS, R21.Pin_1, S11.Pin_1, S11.Pin_2
  N20: Part4.D11_PWM/MOSI, R20.Pin_1, S10.Pin_1, S10.Pin_2
  N21: Part4.D12/MISO, S9.Pin_1, S9.Pin_2, R22.Pin_1
  N22: Part4.D13/SCK, R23.Pin_1, S12.Pin_1, S12.Pin_2
  N23: Part4.D1/TX, LED2.anode
  N24: Part4.D2, LCD2.DB7
  N25: Part4.D3_PWM, LCD2.DB6
  N26: Part4.D4, LCD2.DB5
  N27: Part4.D5_PWM, LCD2.DB4
  N28: Part4.D6_PWM, LCD2.RS
  N29: Part4.D7, LCD2.E
  5V_2: Part4.5V, S9.Pin_3, S9.Pin_4, R24.Pin_1, S10.Pin_3, S10.Pin_4, S11.Pin_3, S11.Pin_4, S12.Pin_3, S12.Pin_4, LCD2.VDD, R26.leg1
  N30: R24.Pin_0, LCD2.LED+
  N31: R25.Pin_1, LED2.cathode
  N32: LCD2.V0, R26.wiper
